# Fritzing sketch Circuit_Design (saved by Fritzing 1.0.6)
breadboards: 1

parts:
  M1 = DOIT Esp32 DevKit v1 (30 pins long, 11 pins width) [part_number=ESP32S-PIN30]
  Part1 = Thumb Joystick
  Part2 = Thumb Joystick
  Grove1 = Grove OLED 128x96
  J1 = Basic Servo
  J2 = Basic Servo
  J3 = Basic Servo
  J4 = Basic Servo
  RE1 = KY-040 Rotary encoder [package=THT]
  U1 = LIPO-1000mAh [package=lipo-1000]

nets:
  VCC: M1.3V3, Part1.VCC, Part2.VCC, Grove1.VCC, RE1.Vcc
  GND: M1.GND, Part1.GND, Part2.GND, Grove1.GND, RE1.GND
  N1: M1.D18, RE1.CLK
  N2: M1.D19, RE1.DT
  N3: M1.D21, Grove1.SDA
  N4: M1.D22, Grove1.SCL
  N5: M1.D34, Part2.VERT
  N6: M1.D35, Part1.HORZ
  N7: M1.D32, Part1.VERT
  VCC_2: M1.VIN, J1.vcc, J2.vcc, J3.vcc, J4.vcc, U1.+
  GND_2: J1.gnd, J2.gnd, J3.gnd, J4.gnd, U1.-

custom parts:
  DOIT Esp32 DevKit v1 (30 pins long, 11 pins width): The DOIT Esp32 DevKit v1 is one of the development board created by DOIT to evaluate the ESP-WROOM-32 module. It is based on the ESP32 microcontroller that boasts Wifi, Bluetooth, Ethernet and Low Power support all in a single chip. (vanepp) made breadboard work, adjusted pin numbering and labels and reduced size of schematic and cleaned up pcb. This chip is 30pins long (2 x15) and 11 pins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
  KY-040 Rotary encoder: KY-040 Rotary Encoder with switch on breakout borad from AZ Delivery
